// Logisim project Controller.circ as structural Verilog: 8 circuits, main circuit Controller
module Controller (
  input  [15:0] Inst,
  input  [3:0] Flags,
  input  Clk,
  input  Reset,
  output Carry,
  output DP_Shift,
  output Imm32_Enable,
  output [4:0] Imm5,
  output [31:0] Imm32,
  output [3:0] ALU_Opcode,
  output [2:0] Rm,
  output [2:0] Rn,
  output [2:0] Rd,
  output [31:0] RAM_Addr,
  output Load,
  output Store,
  output [7:0] PC
);

  wire Conditional_1_verified, Load_Store_1_pc_hold, not_1_out, Opcode_Decoder_1_conditional,
       Opcode_Decoder_1_data_processing, Opcode_Decoder_1_load_store, Opcode_Decoder_1_shift,
       Opcode_Decoder_1_sp_address, Shift_Add_Sub_Mov_1_carry, SP_Address_1_write_enable;
  wire [2:0] Data_Processing_1_rd, Data_Processing_1_rm, Data_Processing_1_rn, Load_Store_1_rd,
       Load_Store_1_rm, Shift_Add_Sub_Mov_1_rd, Shift_Add_Sub_Mov_1_rm, Shift_Add_Sub_Mov_1_rn;
  wire [3:0] Data_Processing_1_alu_opcode, Data_Processing_1_flags_update_mask, flags_apsr_1_flags_out,
       or_1_out, Shift_Add_Sub_Mov_1_alu_opcode, Shift_Add_Sub_Mov_1_flags_update_mask;
  wire [7:0] adder_1_out, adder_2_out, Conditional_1_offset;
  wire [31:0] SP_Address_1_new_stack_pointer, Stack_Pointer_q;

  Register #(.width(32)) Stack_Pointer (
    .D(SP_Address_1_new_stack_pointer), .en(SP_Address_1_write_enable), .clk(Clk), .Q(Stack_Pointer_q),
    .clr(Reset));
  Opcode_Decoder Opcode_Decoder_1 (
    .Opcode(Inst[15:10]), .Shift(Opcode_Decoder_1_shift), .Data_Processing(Opcode_Decoder_1_data_processing),
    .Load_Store(Opcode_Decoder_1_load_store), .SP_Address(Opcode_Decoder_1_sp_address),
    .Conditional(Opcode_Decoder_1_conditional));
  assign or_1_out = Data_Processing_1_flags_update_mask | Shift_Add_Sub_Mov_1_flags_update_mask;  // OR_Gate or_1, 4 bits wide
  Shift_Add_Sub_Mov Shift_Add_Sub_Mov_1 (
    .Imm32_Enable(Imm32_Enable), .Instruction(Inst), .ALU_Opcode(Shift_Add_Sub_Mov_1_alu_opcode),
    .Enable(Opcode_Decoder_1_shift), .Carry(Shift_Add_Sub_Mov_1_carry),
    .Flags_Update_Mask(Shift_Add_Sub_Mov_1_flags_update_mask), .Rd(Shift_Add_Sub_Mov_1_rd),
    .Rn(Shift_Add_Sub_Mov_1_rn), .Rm(Shift_Add_Sub_Mov_1_rm), .Imm5(Imm5), .Imm32(Imm32));
  Data_Processing Data_Processing_1 (
    .Instruction(Inst), .ALU_Opcode(Data_Processing_1_alu_opcode), .Enable(Opcode_Decoder_1_data_processing),
    .Rm(Data_Processing_1_rm), .Rn(Data_Processing_1_rn), .Rd(Data_Processing_1_rd),
    .Flags_Update_Mask(Data_Processing_1_flags_update_mask));
  Flags_APSR flags_apsr_1 (
    .Flags_In(or_1_out), .Update_Mask(Flags), .Clk(Clk), .Rst(Reset), .Flags_Out(flags_apsr_1_flags_out));
  Load_Store Load_Store_1 (
    .Instruction(Inst), .Load(Load), .RAM_Addr(RAM_Addr), .Store(Store), .Stack_Pointer(Stack_Pointer_q),
    .Enable(Opcode_Decoder_1_load_store), .Rd(Load_Store_1_rd), .Rm(Load_Store_1_rm), .Clk(Clk),
    .Reset(Reset), .PC_Hold(Load_Store_1_pc_hold));
  Conditional Conditional_1 (
    .Instruction(Inst), .Verified(Conditional_1_verified), .Enable(Opcode_Decoder_1_conditional),
    .Offset(Conditional_1_offset), .Z(flags_apsr_1_flags_out[2]), .V(flags_apsr_1_flags_out[0]),
    .N(flags_apsr_1_flags_out[3]), .C(flags_apsr_1_flags_out[1]));
  SP_Address SP_Address_1 (
    .New_Stack_Pointer(SP_Address_1_new_stack_pointer), .Stack_Pointer(Stack_Pointer_q),
    .Enable(Opcode_Decoder_1_sp_address), .Instruction(Inst), .Write_Enable(SP_Address_1_write_enable));
  Adder adder_1 (.a(8'h3), .b(Conditional_1_offset), .out(adder_1_out), .cin(1'b0));  // open: cout
  Adder adder_2 (.a(adder_1_out), .b(PC), .out(adder_2_out), .cin(1'b0));  // open: cout
  and and_1 (DP_Shift, Opcode_Decoder_1_shift, ~Opcode_Decoder_1_data_processing);  // AND_Gate
  not not_1 (not_1_out, Load_Store_1_pc_hold);
  Counter counter_1 (
    .clr(Reset), .load(Conditional_1_verified), .up(1'b1), .count(not_1_out), .clk(Clk), .D(adder_2_out),
    .Q(PC));  // open: carry
  Multiplexer #(.enable("false")) multiplexer_1 (
    .in0(flags_apsr_1_flags_out[1]), .in1(Shift_Add_Sub_Mov_1_carry), .out(Carry), .sel(DP_Shift));
  assign ALU_Opcode = Shift_Add_Sub_Mov_1_alu_opcode | Data_Processing_1_alu_opcode;  // OR_Gate or_2, 4 bits wide
  assign Rm = Shift_Add_Sub_Mov_1_rm | Data_Processing_1_rm | Load_Store_1_rm;  // OR_Gate or_3, 3 bits wide
  assign Rn = Shift_Add_Sub_Mov_1_rn | Data_Processing_1_rn;  // OR_Gate or_4, 3 bits wide
  assign Rd = Shift_Add_Sub_Mov_1_rd | Data_Processing_1_rd | Load_Store_1_rd;  // OR_Gate or_5, 3 bits wide

  // Notes on the sheet:
  //   Extract carry
  //   Extract Opcode
  //   IF Reg_Imm=1 THEN use shift value from register ELSE use shift value from Imm5
  //   Buffer flags for next instruction
  //   Add 3 to offset because ARM pre-increments PC
  //   and does an additionnal prefect operation
endmodule

module Conditional (
  input  [15:0] Instruction,
  input  N,
  input  Z,
  input  C,
  input  Enable,
  input  V,
  output [7:0] Offset,
  output Verified
);

  wire and_1_out, and_2_out, and_3_out, comparator_2_eq, multiplexer_1_out, N_Diff_V, N_Egal_V, not_1_out,
       not_2_out, not_3_out, not_4_out, not_5_out, not_6_out, not_7_out, not_8_out, opcode, or_1_out;

  Comparator #(.width(4)) comparator_1 (.a(Instruction[15:12]), .b(4'b1101), .eq(opcode));  // open: gt, lt
  xor xor_1 (N_Diff_V, N, V);
  and and_1 (and_1_out, C, not_1_out);
  not not_1 (not_1_out, Z);
  xnor xnor_1 (N_Egal_V, N, V);
  not not_2 (not_2_out, Z);
  not not_3 (not_3_out, C);
  and and_2 (and_2_out, not_3_out, Z);
  and and_3 (and_3_out, not_2_out, N_Egal_V);
  or or_1 (or_1_out, Z, N_Diff_V);
  not not_4 (not_4_out, Z);
  not not_5 (not_5_out, C);
  not not_6 (not_6_out, N);
  not not_7 (not_7_out, V);
  Multiplexer #(.select(4), .enable("false")) multiplexer_1 (
    .in0(Z), .in1(not_4_out), .in2(C), .in3(not_5_out), .in4(N), .in5(not_6_out), .in6(V), .in7(not_7_out),
    .in8(and_1_out), .in9(and_2_out), .in10(N_Egal_V), .in11(N_Diff_V), .in12(and_3_out), .in13(or_1_out),
    .in14(1'b1), .in15(not_8_out), .out(multiplexer_1_out), .sel(Instruction[11:8]));
  not not_8 (not_8_out, 1'b1);
  Comparator #(.width(1)) comparator_2 (.a(Enable), .b(opcode), .eq(comparator_2_eq));  // open: gt, lt
  and and_4 (Verified, comparator_2_eq, multiplexer_1_out);

  assign Offset = Instruction[7:0];

  // Other names for the same wires on the sheet: CONDITION[3:0] = Instruction[11:8]
endmodule

module Opcode_Decoder (
  input  [5:0] Opcode,
  output Shift,
  output Data_Processing,
  output Load_Store,
  output SP_Address,
  output Conditional
);

  wire not_1_out, not_2_out, not_3_out;

  not not_1 (not_1_out, Opcode[5]);
  not not_2 (not_2_out, Opcode[4]);
  not not_3 (not_3_out, Opcode[3]);
  and and_1 (Shift, not_1_out, not_2_out);
  and and_2 (Data_Processing, not_1_out, Opcode[4]);
  and and_3 (Load_Store, Opcode[5], not_2_out, not_3_out);
  and and_4 (SP_Address, Opcode[5], not_2_out, Opcode[3]);
  and and_5 (Conditional, Opcode[5], Opcode[4]);

  // Other names for the same wires on the sheet: e10 = Opcode[0]; e11 = Opcode[1]; e12 = Opcode[2]; e13 = Opcode[3];
  //   e14 = Opcode[4]; e15 = Opcode[5]

  // Notes on the sheet:
  //   Shift, add, sub, mov
  //   Load/Store
  //   SP Address
  //   Conditional branch
  //   Data Processing
endmodule

module Data_Processing (
  input  Enable,
  input  [15:0] Instruction,
  output [2:0] Rn,
  output [2:0] Rd,
  output [2:0] Rm,
  output [3:0] ALU_Opcode,
  output [3:0] Flags_Update_Mask
);

  wire [2:0] bit_extender_1_out, bit_extender_2_out, bit_extender_3_out, Rd_t, Rn_t;
  wire [3:0] bit_extender_4_out, bit_extender_5_out, multiplexer_3_out;

  Multiplexer #(.select(4), .width(3), .enable("false")) multiplexer_1 (
    .in0(Instruction[15:13]), .in1(Instruction[15:13]), .in2(Instruction[15:13]), .in3(Instruction[15:13]),
    .in4(Instruction[15:13]), .in5(Instruction[15:13]), .in6(Instruction[15:13]), .in7(Instruction[15:13]),
    .in8(3'b000), .in9(Instruction[15:13]), .in10(3'b000), .in11(3'b000), .in12(Instruction[15:13]),
    .in13(Instruction[15:13]), .in14(Instruction[15:13]), .in15(Instruction[15:13]), .out(Rd_t),
    .sel(Instruction[9:6]));
  Multiplexer #(.select(4), .width(3), .enable("false")) multiplexer_2 (
    .in0(Instruction[15:13]), .in1(Instruction[15:13]), .in2(Instruction[15:13]), .in3(Instruction[15:13]),
    .in4(Instruction[15:13]), .in5(Instruction[15:13]), .in6(Instruction[15:13]), .in7(Instruction[15:13]),
    .in8(Instruction[15:13]), .in9(Instruction[15:13]), .in10(Instruction[15:13]), .in11(Instruction[15:13]),
    .in12(Instruction[15:13]), .in13(Instruction[15:13]), .in14(Instruction[15:13]), .in15(3'b000),
    .out(Rn_t), .sel(Instruction[9:6]));
  assign Rn = Rn_t & bit_extender_1_out;  // AND_Gate and_1, 3 bits wide
  assign bit_extender_1_out = {{2{Enable}}, Enable};  // Bit_Extender bit_extender_1
  assign bit_extender_2_out = {{2{Enable}}, Enable};  // Bit_Extender bit_extender_2
  assign bit_extender_3_out = {{2{Enable}}, Enable};  // Bit_Extender bit_extender_3
  assign bit_extender_4_out = {{3{Enable}}, Enable};  // Bit_Extender bit_extender_4
  Multiplexer #(.select(4), .width(4), .enable("false")) multiplexer_3 (
    .in0(4'b1110), .in1(4'b1110), .in2(4'b1110), .in3(4'b1110), .in4(4'b1110), .in5(4'b1111), .in6(4'b1111),
    .in7(4'b1110), .in9(4'b1111), .in10(4'b1111), .in11(4'b1111), .in12(4'b1110), .in13(4'b1100),
    .in14(4'b1110), .in15(4'b1110), .out(multiplexer_3_out), .sel(Instruction[9:6]));  // open: in8
  assign Rd = Rd_t & bit_extender_2_out;  // AND_Gate and_2, 3 bits wide
  assign Rm = Instruction[12:10] & bit_extender_3_out;  // AND_Gate and_3, 3 bits wide
  assign ALU_Opcode = Instruction[9:6] & bit_extender_4_out;  // AND_Gate and_4, 4 bits wide
  assign bit_extender_5_out = {{3{Enable}}, Enable};  // Bit_Extender bit_extender_5
  assign Flags_Update_Mask = bit_extender_5_out & multiplexer_3_out;  // AND_Gate and_5, 4 bits wide

  // Other names for the same wires on the sheet: OP[3:0] = Instruction[9:6]; Rm_t[2:0] = Instruction[12:10];
  //   Rdn[2:0] = Instruction[15:13]

  // Notes on the sheet:
  //   Pull output low on Enable = 0
  //   Note 2: RSB instruction has Rn as 1st operand.
  //   MUL instruction has Rn as 1st operand and Rdm as 2nd operand
  //   Pull output low on Enable = 0
  //   For simplification purposes, Rm is used for 1st operand both here and in the ALU.
  //   Note: instructions that does not save the result will still have the second operand as the destination register, the ALU will copy the second register to the destination register
endmodule

module Shift_Add_Sub_Mov (
  input  [15:0] Instruction,
  input  Enable,
  output [3:0] ALU_Opcode,
  output [3:0] Flags_Update_Mask,
  output Carry,
  output Imm32_Enable,
  output [2:0] Rm,
  output [2:0] Rn,
  output [2:0] Rd,
  output [4:0] Imm5,
  output [31:0] Imm32
);


  // Notes on the sheet:
  //   Pull output low on Enable = 0
  //   Note: ALU uses Rn register for shifts. Use Rn instead of Rm for shifts (immediate) here too
  //   Note 2: MOV uses RSB ALU opcode with Imm8 reversed so that it is copied to output register
  //   Note 3: Imm32_Enable forces the use of the immediate for Rm register
  //   Enable carry for SUB since it is reversed in ALU
  //   ALU will use Imm32 instead of Rm
endmodule

module Load_Store (
  input  [15:0] Instruction,
  input  [31:0] Stack_Pointer,
  input  Enable,
  input  Clk,
  input  Reset,
  output Store,
  output Load,
  output [2:0] Rm,
  output [2:0] Rd,
  output [31:0] RAM_Addr,
  output PC_Hold
);

  wire and_1_out, d_ff_1_q, d_ff_1_qn, not_1_out;
  wire [2:0] bit_extender_3_out;
  wire [31:0] adder_1_out, bit_extender_1_out, bit_extender_2_out, register_1_q;

  Adder #(.width(32)) adder_1 (.a(Stack_Pointer), .b(bit_extender_1_out), .out(adder_1_out));  // open: cin, cout
  assign bit_extender_1_out = {{24{1'b0}}, Instruction[7:0]};  // Bit_Extender bit_extender_1
  D_Flip_Flop d_ff_1 (.D(and_1_out), .clk(Clk), .Q(d_ff_1_q), .Qn(d_ff_1_qn), .reset(Reset));  // open: preset
  and and_1 (and_1_out, d_ff_1_qn, Instruction[11]);
  Register #(.width(32)) register_1 (.D(adder_1_out), .en(Enable), .clk(Clk), .Q(register_1_q), .clr(Reset));
  assign bit_extender_2_out = {{31{Enable}}, Enable};  // Bit_Extender bit_extender_2
  not not_1 (not_1_out, Instruction[11]);
  assign bit_extender_3_out = {{2{Enable}}, Enable};  // Bit_Extender bit_extender_3
  assign RAM_Addr = register_1_q & bit_extender_2_out;  // AND_Gate and_2, 32 bits wide
  and and_3 (Store, not_1_out, Enable);
  and and_4 (Load, Instruction[11], Enable);
  assign Rd = Instruction[10:8] & bit_extender_3_out;  // AND_Gate and_5, 3 bits wide
  and and_6 (PC_Hold, d_ff_1_q, Enable);

  assign Rm = Rd;

  // Other names for the same wires on the sheet: E = Enable; Imm[7:0] = Instruction[7:0]; R[2:0] = Instruction[10:8];
  //   a = Instruction[11]

  // Notes on the sheet:
  //   Delay load and hold PC for 1 cycle for the RAM to send out requested data 
endmodule

module SP_Address (
  input  Enable,
  input  [15:0] Instruction,
  input  [31:0] Stack_Pointer,
  output Write_Enable,
  output [31:0] New_Stack_Pointer
);


  // Notes on the sheet:
  //   Pull output low on Enable = 0
endmodule

module Flags_APSR (
  input  [3:0] Flags_In,
  input  [3:0] Update_Mask,
  input  Clk,
  input  Rst,
  output [3:0] Flags_Out
);

  Register #(.width(1)) register_1 (.D(Flags_In[0]), .en(Update_Mask[0]), .clk(Clk), .Q(Flags_Out[0]), .clr(Rst));
  Register #(.width(1)) register_2 (.D(Flags_In[1]), .en(Update_Mask[1]), .clk(Clk), .Q(Flags_Out[1]), .clr(Rst));
  Register #(.width(1)) register_3 (.D(Flags_In[2]), .en(Update_Mask[2]), .clk(Clk), .Q(Flags_Out[2]), .clr(Rst));
  Register #(.width(1)) register_4 (.D(Flags_In[3]), .en(Update_Mask[3]), .clk(Clk), .Q(Flags_Out[3]), .clr(Rst));

  // Other names for the same wires on the sheet: Reset = Rst
endmodule
